# Fritzing sketch Arduino sketch BR (saved by Fritzing 1.0.5)
breadboards: 1

parts:
  Part1 = Arduino Uno (Rev3) - ICSP
  S1 = Square Pushbutton
  R1 = Resistor [tolerance=±5% power=0.25W resistance=10000 package=THT]
  HC-SR04_Sensor_1 = HC-SR04 Ultrasonic Distance Sensor

nets:
  5V: Part1.5V, S1.leg0, HC-SR04_Sensor_1.VCC
  GND: Part1.GND, R1.Pin_1, HC-SR04_Sensor_1.GND
  N1: Part1.D9_PWM, HC-SR04_Sensor_1.TRIG
  N2: Part1.D10_PWM/SS, HC-SR04_Sensor_1.ECHO
  N3: Part1.D2, S1.leg1, R1.Pin_0
